// Logisim project clock circuit.circ as structural Verilog: 6 circuits, main circuit main
module main (
  input  in_1,
  input  AM_PM_switch,
  output out_3,
  output out_4
);

  wire _12_or_24_out_7, _12_or_24_out_8, _12_or_24_out_9, _12_or_24_out_10, _12_or_24_out_11,
       _12_or_24_out_12, _12_or_24_out_13, _12_or_24_out_14, clock_1_out, decoder_2_out_5, decoder_2_out_6,
       decoder_2_out_7, decoder_2_out_8, decoder_2_out_9, decoder_2_out_10, decoder_2_out_11,
       decoder_3_out_5, decoder_3_out_6, decoder_3_out_7, decoder_3_out_8, decoder_3_out_9, decoder_3_out_10,
       decoder_3_out_11, decoder_4_out_5, decoder_4_out_6, decoder_4_out_7, decoder_4_out_8, decoder_4_out_9,
       decoder_4_out_10, decoder_4_out_11, decoder_5_out_5, decoder_5_out_6, decoder_5_out_7,
       decoder_5_out_8, decoder_5_out_9, decoder_5_out_10, decoder_5_out_11, decoder_6_out_5,
       decoder_6_out_6, decoder_6_out_7, decoder_6_out_8, decoder_6_out_9, decoder_6_out_10,
       decoder_6_out_11, decoder_out_5, decoder_out_6, decoder_out_7, decoder_out_8, decoder_out_9,
       decoder_out_10, decoder_out_11, plus_1_2_out, plus_1_3_out, plus_1_out, plus_10_2_out, plus_10_out,
       sec_min_2_out_5, sec_min_2_out_6, sec_min_2_out_7, sec_min_2_out_8, sec_min_2_out_9, sec_min_2_out_10,
       sec_min_2_out_11, sec_min_2_out_12, sec_min_2_out_13, sec_min_out_5, sec_min_out_6, sec_min_out_7,
       sec_min_out_8, sec_min_out_9, sec_min_out_10, sec_min_out_11, sec_min_out_12, sec_min_out_13;

  Clock clock_1 (.out(clock_1_out));
  Sec_min sec_min (
    .in_1(in_1), .in_2(clock_1_out), .out_5(sec_min_out_5), .out_6(sec_min_out_6), .out_7(sec_min_out_7),
    .out_8(sec_min_out_8), .out_9(sec_min_out_9), .out_10(sec_min_out_10), .out_11(sec_min_out_11),
    .out_12(sec_min_out_12), .out_13(sec_min_out_13), .in_3(plus_10_out), .in_4(plus_1_out));
  decoder decoder (
    .Q(sec_min_out_10), .W(sec_min_out_11), .E(sec_min_out_12), .R(sec_min_out_13), .out_5(decoder_out_5),
    .out_6(decoder_out_6), .out_7(decoder_out_7), .out_8(decoder_out_8), .out_9(decoder_out_9),
    .out_10(decoder_out_10), .out_11(decoder_out_11));
  decoder decoder_2 (
    .Q(sec_min_out_6), .W(sec_min_out_7), .E(sec_min_out_8), .R(sec_min_out_9), .out_5(decoder_2_out_5),
    .out_6(decoder_2_out_6), .out_7(decoder_2_out_7), .out_8(decoder_2_out_8), .out_9(decoder_2_out_9),
    .out_10(decoder_2_out_10), .out_11(decoder_2_out_11));
  _7_Segment_Display u_7_segment_display_1 (
    .g(decoder_2_out_5), .f(decoder_2_out_6), .a(decoder_2_out_7), .b(decoder_2_out_8), .e(decoder_2_out_11),
    .d(decoder_2_out_10), .c(decoder_2_out_9));  // open: dp
  _7_Segment_Display u_7_segment_display_2 (
    .g(decoder_out_5), .f(decoder_out_6), .a(decoder_out_7), .b(decoder_out_8), .e(decoder_out_11),
    .d(decoder_out_10), .c(decoder_out_9));  // open: dp
  Button plus_10 (.out(plus_10_out));
  Button plus_1 (.out(plus_1_out));
  Sec_min sec_min_2 (
    .in_1(in_1), .in_2(sec_min_out_5), .out_5(sec_min_2_out_5), .out_6(sec_min_2_out_6),
    .out_7(sec_min_2_out_7), .out_8(sec_min_2_out_8), .out_9(sec_min_2_out_9), .out_10(sec_min_2_out_10),
    .out_11(sec_min_2_out_11), .out_12(sec_min_2_out_12), .out_13(sec_min_2_out_13), .in_3(plus_10_2_out),
    .in_4(plus_1_2_out));
  decoder decoder_3 (
    .Q(sec_min_2_out_10), .W(sec_min_2_out_11), .E(sec_min_2_out_12), .R(sec_min_2_out_13),
    .out_5(decoder_3_out_5), .out_6(decoder_3_out_6), .out_7(decoder_3_out_7), .out_8(decoder_3_out_8),
    .out_9(decoder_3_out_9), .out_10(decoder_3_out_10), .out_11(decoder_3_out_11));
  decoder decoder_4 (
    .Q(sec_min_2_out_6), .W(sec_min_2_out_7), .E(sec_min_2_out_8), .R(sec_min_2_out_9),
    .out_5(decoder_4_out_5), .out_6(decoder_4_out_6), .out_7(decoder_4_out_7), .out_8(decoder_4_out_8),
    .out_9(decoder_4_out_9), .out_10(decoder_4_out_10), .out_11(decoder_4_out_11));
  _7_Segment_Display u_7_segment_display_3 (
    .g(decoder_4_out_5), .f(decoder_4_out_6), .a(decoder_4_out_7), .b(decoder_4_out_8), .e(decoder_4_out_11),
    .d(decoder_4_out_10), .c(decoder_4_out_9));  // open: dp
  _7_Segment_Display u_7_segment_display_4 (
    .g(decoder_3_out_5), .f(decoder_3_out_6), .a(decoder_3_out_7), .b(decoder_3_out_8), .e(decoder_3_out_11),
    .d(decoder_3_out_10), .c(decoder_3_out_9));  // open: dp
  Button plus_10_2 (.out(plus_10_2_out));
  Button plus_1_2 (.out(plus_1_2_out));
  decoder decoder_5 (
    .Q(_12_or_24_out_10), .W(_12_or_24_out_9), .E(_12_or_24_out_8), .R(_12_or_24_out_7),
    .out_5(decoder_5_out_5), .out_6(decoder_5_out_6), .out_7(decoder_5_out_7), .out_8(decoder_5_out_8),
    .out_9(decoder_5_out_9), .out_10(decoder_5_out_10), .out_11(decoder_5_out_11));
  decoder decoder_6 (
    .Q(_12_or_24_out_14), .W(_12_or_24_out_13), .E(_12_or_24_out_12), .R(_12_or_24_out_11),
    .out_5(decoder_6_out_5), .out_6(decoder_6_out_6), .out_7(decoder_6_out_7), .out_8(decoder_6_out_8),
    .out_9(decoder_6_out_9), .out_10(decoder_6_out_10), .out_11(decoder_6_out_11));
  _12or24 _12_or_24 (
    .in_2(in_1), .in_4(sec_min_2_out_5), .in_1(AM_PM_switch), .out_14(_12_or_24_out_14),
    .out_13(_12_or_24_out_13), .out_12(_12_or_24_out_12), .out_11(_12_or_24_out_11),
    .out_10(_12_or_24_out_10), .out_9(_12_or_24_out_9), .out_8(_12_or_24_out_8), .out_7(_12_or_24_out_7),
    .out_5(out_3), .out_6(out_4), .in_3(plus_1_3_out));
  _7_Segment_Display u_7_segment_display_5 (
    .g(decoder_6_out_5), .f(decoder_6_out_6), .a(decoder_6_out_7), .b(decoder_6_out_8), .e(decoder_6_out_11),
    .d(decoder_6_out_10), .c(decoder_6_out_9));  // open: dp
  _7_Segment_Display u_7_segment_display_6 (
    .g(decoder_5_out_5), .f(decoder_5_out_6), .a(decoder_5_out_7), .b(decoder_5_out_8), .e(decoder_5_out_11),
    .d(decoder_5_out_10), .c(decoder_5_out_9));  // open: dp
  Button plus_1_3 (.out(plus_1_3_out));
endmodule

module Sec_min (
  input  in_1,
  input  in_2,
  input  in_3,
  input  in_4,
  output out_5,
  output out_6,
  output out_7,
  output out_8,
  output out_9,
  output out_10,
  output out_11,
  output out_12,
  output out_13
);

  wire and_2_out, buffer_1_out, buffer_2_out, not_1_out, not_2_out, not_3_out, not_5_out, not_6_out,
       not_7_out, not_8_out, not_9_out, not_10_out, or_1_out, or_2_out;

  T_Flip_Flop t_ff_1 (.clk(not_1_out), .T(in_1), .Q(out_7), .reset(buffer_1_out));  // open: Qn, preset, en
  not not_1 (not_1_out, out_8);
  not not_2 (not_2_out, out_9);
  T_Flip_Flop t_ff_2 (.clk(not_2_out), .T(in_1), .Q(out_8), .reset(buffer_1_out));  // open: Qn, preset, en
  T_Flip_Flop t_ff_3 (.clk(not_3_out), .T(in_1), .Q(out_9), .reset(buffer_1_out));  // open: Qn, preset, en
  not not_3 (not_3_out, or_2_out);
  not not_4 (out_6, in_1);
  and and_1 (out_5, out_7, out_8, not_5_out);
  not not_5 (not_5_out, out_9);
  buf buffer_1 (buffer_1_out, out_5);
  not not_6 (not_6_out, out_11);
  not not_7 (not_7_out, out_12);
  not not_8 (not_8_out, out_13);
  or or_1 (or_1_out, in_2, in_4);
  T_Flip_Flop t_ff_4 (.clk(not_6_out), .T(in_1), .Q(out_10), .reset(buffer_2_out));  // open: Qn, preset, en
  T_Flip_Flop t_ff_5 (.clk(not_7_out), .T(in_1), .Q(out_11), .reset(buffer_2_out));  // open: Qn, preset, en
  T_Flip_Flop t_ff_6 (.clk(not_8_out), .T(in_1), .Q(out_12), .reset(buffer_2_out));  // open: Qn, preset, en
  T_Flip_Flop t_ff_7 (.clk(or_1_out), .T(in_1), .Q(out_13), .reset(buffer_2_out));  // open: Qn, preset, en
  not not_9 (not_9_out, out_11);
  not not_10 (not_10_out, out_13);
  or or_2 (or_2_out, and_2_out, in_3);
  and and_2 (and_2_out, out_10, not_9_out, out_12, not_10_out);
  buf buffer_2 (buffer_2_out, and_2_out);
endmodule

module _24hour (
  input  in_1,
  input  in_2,
  input  in_3,
  output out_4,
  output out_5,
  output out_6,
  output out_7,
  output out_8,
  output out_9,
  output out_10,
  output out_11
);

  wire and_1_out, and_2_out, and_3_out, not_1_out, not_2_out, not_4_out, not_5_out, not_6_out, not_7_out,
       not_8_out, not_9_out, not_10_out, not_11_out, not_12_out, not_13_out, or_1_out, or_2_out;

  not not_1 (not_1_out, out_7);
  T_Flip_Flop t_ff_1 (.clk(not_1_out), .T(in_1), .Q(out_6), .reset(and_1_out));  // open: Qn, preset, en
  T_Flip_Flop t_ff_2 (.clk(not_2_out), .T(in_1), .Q(out_7), .reset(and_1_out));  // open: Qn, preset, en
  not not_2 (not_2_out, and_3_out);
  not not_3 (out_4, in_1);
  and and_1 (and_1_out, out_6, not_4_out, not_7_out, not_6_out, out_9, not_5_out);
  not not_4 (not_4_out, out_7);
  not not_5 (not_5_out, out_8);
  not not_6 (not_6_out, out_10);
  not not_7 (not_7_out, out_11);
  not not_8 (not_8_out, out_9);
  buf and_2 (and_2_out, or_2_out);  // AND_Gate
  not not_9 (not_9_out, out_10);
  not not_10 (not_10_out, out_11);
  or or_1 (or_1_out, in_2, in_3);
  not not_11 (not_11_out, or_1_out);
  T_Flip_Flop t_ff_3 (.clk(not_8_out), .T(in_1), .Q(out_8), .reset(and_2_out));  // open: Qn, preset, en
  T_Flip_Flop t_ff_4 (.clk(not_9_out), .T(in_1), .Q(out_9), .reset(or_2_out));  // open: Qn, preset, en
  T_Flip_Flop t_ff_5 (.clk(not_10_out), .T(in_1), .Q(out_10), .reset(or_2_out));  // open: Qn, preset, en
  T_Flip_Flop t_ff_6 (.clk(not_11_out), .T(in_1), .Q(out_11), .reset(or_2_out));  // open: Qn, preset, en
  and and_3 (and_3_out, out_8, not_12_out, out_10, not_13_out);
  not not_12 (not_12_out, out_9);
  not not_13 (not_13_out, out_11);
  or or_2 (or_2_out, and_3_out, and_1_out);

  assign out_5 = out_4;
endmodule

module _12hour (
  input  in_1,
  input  in_2,
  input  in_3,
  output out_4,
  output out_5,
  output out_6,
  output out_7,
  output out_8,
  output out_9,
  output out_10
);

  wire and_1_out, and_2_out, buffer_1_out, not_1_out, not_2_out, not_3_out, not_4_out, not_5_out, not_6_out,
       not_7_out, not_8_out, not_9_out, not_10_out, or_1_out, or_2_out;

  not not_1 (not_1_out, buffer_1_out);
  T_Flip_Flop t_ff_1 (.clk(not_1_out), .T(in_1), .Q(out_4), .reset(or_2_out));  // open: Qn, preset, en
  or or_1 (or_1_out, in_2, in_3);
  not not_2 (not_2_out, out_6);
  not not_3 (not_3_out, out_7);
  not not_4 (not_4_out, out_8);
  T_Flip_Flop t_ff_2 (.clk(and_2_out), .T(in_1), .Q(out_9), .Qn(out_10));  // open: preset, reset, en
  T_Flip_Flop t_ff_3 (.clk(not_2_out), .T(in_1), .Q(out_5), .reset(or_2_out));  // open: Qn, preset, en
  T_Flip_Flop t_ff_4 (.clk(not_3_out), .T(in_1), .Q(out_6), .reset(or_2_out));  // open: Qn, preset, en
  T_Flip_Flop t_ff_5 (.clk(not_4_out), .T(in_1), .Q(out_7), .reset(or_2_out));  // open: Qn, preset, en
  not not_5 (not_5_out, or_1_out);
  T_Flip_Flop t_ff_6 (.clk(not_5_out), .T(in_1), .Q(out_8), .reset(or_2_out));  // open: Qn, preset, en
  not not_6 (not_6_out, out_6);
  not not_7 (not_7_out, out_8);
  not not_8 (not_8_out, out_5);
  not not_9 (not_9_out, out_6);
  not not_10 (not_10_out, out_8);
  buf buffer_1 (buffer_1_out, and_1_out);
  and and_1 (and_1_out, out_5, not_6_out, out_7, not_7_out);
  and and_2 (and_2_out, not_8_out, not_9_out, out_7, not_10_out, out_4);
  or or_2 (or_2_out, and_2_out, buffer_1_out);
endmodule

module _12or24 (
  input  in_1,
  input  in_2,
  input  in_3,
  input  in_4,
  output out_5,
  output out_6,
  output out_7,
  output out_8,
  output out_9,
  output out_10,
  output out_11,
  output out_12,
  output out_13,
  output out_14
);

  wire n12hour_1_out_4, n12hour_1_out_5, n12hour_1_out_6, n12hour_1_out_7, n12hour_1_out_8, n12hour_1_out_9,
       n12hour_1_out_10, n24hour_1_out_4, n24hour_1_out_5, n24hour_1_out_6, n24hour_1_out_7, n24hour_1_out_8,
       n24hour_1_out_9, n24hour_1_out_10, n24hour_1_out_11, not_1_out, not_2_out, not_3_out, not_4_out,
       not_5_out;

  _24hour u_24hour_1 (
    .in_1(in_2), .in_2(in_4), .out_4(n24hour_1_out_4), .out_5(n24hour_1_out_5), .out_6(n24hour_1_out_6),
    .out_7(n24hour_1_out_7), .out_8(n24hour_1_out_8), .out_9(n24hour_1_out_9), .out_10(n24hour_1_out_10),
    .out_11(n24hour_1_out_11), .in_3(in_3));
  _12hour u_12hour_1 (
    .in_1(in_2), .in_2(in_4), .out_4(n12hour_1_out_4), .out_5(n12hour_1_out_5), .out_6(n12hour_1_out_6),
    .out_7(n12hour_1_out_7), .out_8(n12hour_1_out_8), .out_10(n12hour_1_out_10), .out_9(n12hour_1_out_9),
    .in_3(in_3));
  not not_1 (not_1_out, in_2);
  not not_2 (not_2_out, in_2);
  not not_3 (not_3_out, in_2);
  Multiplexer multiplexer_1 (.in0(n12hour_1_out_8), .in1(n24hour_1_out_11), .out(out_7), .sel(in_1));  // open: en
  Multiplexer multiplexer_2 (.in0(n12hour_1_out_7), .in1(n24hour_1_out_10), .out(out_8), .sel(in_1));  // open: en
  Multiplexer multiplexer_3 (.in0(n12hour_1_out_6), .in1(n24hour_1_out_9), .out(out_9), .sel(in_1));  // open: en
  Multiplexer multiplexer_4 (.in0(n12hour_1_out_5), .in1(n24hour_1_out_8), .out(out_10), .sel(in_1));  // open: en
  Multiplexer multiplexer_5 (.in0(n12hour_1_out_4), .in1(n24hour_1_out_7), .out(out_11), .sel(in_1));  // open: en
  Multiplexer multiplexer_6 (.in0(not_1_out), .in1(n24hour_1_out_6), .out(out_12), .sel(in_1));  // open: en
  Multiplexer multiplexer_7 (.in0(not_2_out), .in1(n24hour_1_out_5), .out(out_13), .sel(in_1));  // open: en
  Multiplexer multiplexer_8 (.in0(not_3_out), .in1(n24hour_1_out_4), .out(out_14), .sel(in_1));  // open: en
  and and_1 (out_5, n12hour_1_out_10, not_5_out);
  not not_4 (not_4_out, in_1);
  not not_5 (not_5_out, in_1);
  and and_2 (out_6, n12hour_1_out_9, not_4_out);
endmodule

module decoder (
  input  Q,
  input  W,
  input  E,
  input  R,
  output out_5,
  output out_6,
  output out_7,
  output out_8,
  output out_9,
  output out_10,
  output out_11
);

  wire and_1_out, and_2_out, nor_1_out, nor_2_out, nor_3_out, not_1_out, not_2_out, not_3_out, not_4_out,
       not_5_out, xnor_1_out, xnor_2_out, xnor_3_out, xor_1_out, xor_2_out, xor_3_out;

  and and_1 (and_1_out, E, not_1_out);
  not not_1 (not_1_out, R);
  ExactlyOne xor_1 (.out(xor_1_out), .in0(Q), .in1(W), .in2(E));
  nor nor_1 (nor_1_out, E, R);
  xnor xnor_1 (xnor_1_out, W, R);
  not not_2 (not_2_out, W);
  xnor xnor_2 (xnor_2_out, E, R);
  not not_3 (not_3_out, W);
  not not_4 (not_4_out, R);
  xor xor_2 (xor_2_out, Q, W);
  xor xor_3 (xor_3_out, E, R);
  nor nor_2 (nor_2_out, W, R);
  nor nor_3 (nor_3_out, W, R);
  and and_2 (and_2_out, E, not_5_out);
  not not_5 (not_5_out, R);
  or or_1 (out_5, and_1_out, xor_1_out);
  or or_2 (out_6, Q, W, nor_1_out);
  or or_3 (out_7, Q, E, xnor_1_out);
  or or_4 (out_8, not_2_out, xnor_2_out);
  nand nand_1 (out_9, E, not_3_out, not_4_out);
  xnor xnor_3 (xnor_3_out, xor_2_out, xor_3_out);
  or or_5 (out_11, nor_3_out, and_2_out);
  or or_6 (out_10, xnor_3_out, nor_2_out);
endmodule
