// Logisim project electrical fan final cirucuit.circ as structural Verilog: 13 circuits, main circuit main
module main (
  input  _12_24h_switch,
  input  Main_Power,
  output AM,
  output PM
);

  wire and_1_out, button_1_out, button_2_out, button_3_out, button_4_out, clock_1_out, fan_pwer_1_leve1_led,
       fan_pwer_1_level2_led, fan_pwer_1_level3_led, fan_pwer_1_rotation, hour_out_6, hour_out_7, hour_out_8,
       hour_out_9, hour_out_10, hour_out_11, hour_out_12, hour_out_13, hour_out_15, hour_out_16, hour_out_17,
       hour_out_18, hour_out_19, hour_out_20, min_out_6, min_out_7, min_out_8, min_out_9, min_out_10,
       min_out_11, min_out_12, min_out_13, min_out_14, min_out_15, min_out_16, min_out_17, min_out_18,
       min_out_19, min_plus_hour, not_1_out, or_1_out, plus_1_2_out, plus_1_3_out, plus_1_out, plus_10_2_out,
       plus_10_out, plus_30m_out, register_1_q, reset_out, sec_out_5, sec_out_6, sec_out_7, sec_out_8,
       sec_out_9, sec_out_10, sec_out_11, sec_out_12, sec_out_13, sec_out_14, sec_out_15, sec_out_16,
       sec_out_17, sec_out_18, sec_plus_min, start_out, timer_main_1_out_11, xor_1_out;
  wire [3:0] timer_main_1_h_re, timer_main_1_h_set, timer_main_1_m1_re, timer_main_1_m1_set,
       timer_main_1_m10_re, timer_main_1_m10_set;

  xor xor_1 (xor_1_out, Main_Power, and_1_out);
  Button button_1 (.out(button_1_out));
  Button plus_10 (.out(plus_10_out));
  Button plus_1 (.out(plus_1_out));
  Button button_2 (.out(button_2_out));
  Button button_3 (.out(button_3_out));
  sec_clk sec (
    .power(Main_Power), .plus_min(sec_plus_min), .out_12(sec_out_12), .out_13(sec_out_13),
    .out_14(sec_out_14), .out_15(sec_out_15), .out_16(sec_out_16), .out_17(sec_out_17), .out_18(sec_out_18),
    .out_5(sec_out_5), .out_6(sec_out_6), .out_7(sec_out_7), .out_8(sec_out_8), .out_9(sec_out_9),
    .out_10(sec_out_10), .out_11(sec_out_11), .plus_10(plus_10_out), .plus_1(plus_1_out));
  _7_Segment_Display u_7_segment_display_1 (
    .g(sec_out_15), .f(sec_out_16), .a(sec_out_17), .b(sec_out_18), .e(sec_out_12), .d(sec_out_13),
    .c(sec_out_14));  // open: dp
  _7_Segment_Display u_7_segment_display_2 (
    .g(sec_out_8), .f(sec_out_9), .a(sec_out_10), .b(sec_out_11), .e(sec_out_5), .d(sec_out_6), .c(sec_out_7));  // open: dp
  fan_pwer fan_pwer_1 (
    .in_1(xor_1_out), .in_2(button_1_out), .in_3(button_3_out), .in_4(button_2_out), .in_5(button_4_out),
    .Leve1_LED(fan_pwer_1_leve1_led), .Level2_LED(fan_pwer_1_level2_led), .Level3_LED(fan_pwer_1_level3_led),
    .Rotation(fan_pwer_1_rotation));
  Button button_4 (.out(button_4_out));
  Button plus_10_2 (.out(plus_10_2_out));
  LED led_1 (.in(fan_pwer_1_level2_led));
  LED led_2 (.in(fan_pwer_1_leve1_led));
  _7_Segment_Display u_7_segment_display_3 (
    .g(min_out_6), .f(min_out_7), .a(min_out_8), .b(min_out_9), .e(min_out_14), .d(min_out_15), .c(min_out_16));  // open: dp
  Button plus_1_2 (.out(plus_1_2_out));
  LED led_3 (.in(fan_pwer_1_level3_led));
  min_clk min (
    .power(Main_Power), .plus_min(sec_plus_min), .plus_hour(min_plus_hour), .out_14(min_out_14),
    .out_15(min_out_15), .out_16(min_out_16), .out_6(min_out_6), .out_7(min_out_7), .out_8(min_out_8),
    .out_9(min_out_9), .out_17(min_out_17), .out_18(min_out_18), .out_19(min_out_19), .out_10(min_out_10),
    .out_11(min_out_11), .out_12(min_out_12), .out_13(min_out_13), .plus_10(plus_10_2_out),
    .plus_1(plus_1_2_out));
  _7_Segment_Display u_7_segment_display_4 (
    .g(min_out_10), .f(min_out_11), .a(min_out_12), .b(min_out_13), .e(min_out_17), .d(min_out_18),
    .c(min_out_19));  // open: dp
  LED led_4 (.in(fan_pwer_1_rotation));
  Button plus_1_3 (.out(plus_1_3_out));
  or or_1 (or_1_out, fan_pwer_1_leve1_led, fan_pwer_1_level2_led, fan_pwer_1_level3_led);
  _7_Segment_Display u_7_segment_display_5 (
    .g(hour_out_6), .f(hour_out_7), .a(hour_out_8), .b(hour_out_9), .e(hour_out_15), .d(hour_out_16),
    .c(hour_out_17));  // open: dp
  Hex_Digit_Display hex_digit_display_1 (.value(timer_main_1_h_set));  // open: dp
  hour_clk hour (
    ._12_24(_12_24h_switch), .power(Main_Power), .plus_1hour(min_plus_hour), .am(AM), .pm(PM),
    .out_15(hour_out_15), .out_16(hour_out_16), .out_17(hour_out_17), .out_6(hour_out_6), .out_7(hour_out_7),
    .out_8(hour_out_8), .out_9(hour_out_9), .out_18(hour_out_18), .out_19(hour_out_19), .out_20(hour_out_20),
    .out_10(hour_out_10), .out_11(hour_out_11), .out_12(hour_out_12), .out_13(hour_out_13),
    .plus_1(plus_1_3_out));
  _7_Segment_Display u_7_segment_display_6 (
    .g(hour_out_10), .f(hour_out_11), .a(hour_out_12), .b(hour_out_13), .e(hour_out_18), .d(hour_out_19),
    .c(hour_out_20));  // open: dp
  Hex_Digit_Display hex_digit_display_2 (.value(timer_main_1_m1_set));  // open: dp
  Hex_Digit_Display hex_digit_display_3 (.value(timer_main_1_m10_set));  // open: dp
  Button plus_30m (.out(plus_30m_out));
  Hex_Digit_Display hex_digit_display_4 (.value(timer_main_1_h_re));  // open: dp
  timer_main timer_main_1 (
    .add30(plus_30m_out), .timer_start(start_out), .h_set(timer_main_1_h_set),
    .m10_set(timer_main_1_m10_set), .m1_set(timer_main_1_m1_set), .h_re(timer_main_1_h_re),
    .m10_re(timer_main_1_m10_re), .m1_re(timer_main_1_m1_re), .out_11(timer_main_1_out_11), .power(or_1_out),
    .reset(reset_out));
  Button reset (.out(reset_out));
  Button start (.out(start_out));
  Hex_Digit_Display hex_digit_display_5 (.value(timer_main_1_m10_re));  // open: dp
  Hex_Digit_Display hex_digit_display_6 (.value(timer_main_1_m1_re));  // open: dp
  not not_1 (not_1_out, timer_main_1_out_11);
  and and_1 (and_1_out, not_1_out, register_1_q);
  Register #(.width(1)) register_1 (.D(timer_main_1_out_11), .Q(register_1_q), .clk(clock_1_out));  // open: en, clr
  Clock clock_1 (.out(clock_1_out));

  // Notes on the sheet:
  //   Level1
  //   Level3
  //   Level2
  //   Rotation
  //   Level1
  //   Level2
  //   Level3
  //   Rotation
  //   Time Setting
  //   Remaining
endmodule

module timer_main (
  input  add30,
  input  power,
  input  timer_start,
  input  reset,
  output [3:0] h_set,
  output [3:0] m10_set,
  output [3:0] m1_set,
  output [3:0] h_re,
  output [3:0] m10_re,
  output [3:0] m1_re,
  output out_11
);

  wire clock_1_out, comparator_1_eq, not_1_out, not_2_out, or_1_out, xor_1_out;
  wire [8:0] counter_1_q, set_time_1_out_3;

  Clock #(.lowDuration(59)) clock_1 (.out(clock_1_out));
  not not_1 (not_1_out, timer_start);
  set_time set_time_1 (.add30(add30), .out_3(set_time_1_out_3), .power(power));
  or or_1 (or_1_out, timer_start, clock_1_out);
  timer_dec timer_dec_1 (.in_1(set_time_1_out_3), .out_2(h_set), .out_3(m10_set), .out_4(m1_set));
  not not_2 (not_2_out, power);
  xor xor_1 (xor_1_out, not_2_out, reset);
  Counter #(.width(9), .max('h1ff), .ongoal("stay")) counter_1 (
    .load(1'b1), .D(set_time_1_out_3), .count(not_1_out), .Q(counter_1_q), .clk(or_1_out), .clr(xor_1_out));  // open: carry
  timer_dec timer_dec_2 (.in_1(counter_1_q), .out_2(h_re), .out_3(m10_re), .out_4(m1_re));
  Comparator #(.width(9)) comparator_1 (.a(counter_1_q), .b({9{1'b0}}), .eq(comparator_1_eq));  // open: gt, lt
  not not_3 (out_11, comparator_1_eq);
endmodule

module Sec_min (
  input  in_1,
  input  in_2,
  input  in_3,
  input  in_4,
  output out_5,
  output out_6,
  output out_7,
  output out_8,
  output out_9,
  output out_10,
  output out_11,
  output out_12,
  output out_13
);

  wire and_2_out, buffer_1_out, buffer_2_out, not_1_out, not_2_out, not_3_out, not_5_out, not_6_out,
       not_7_out, not_8_out, not_9_out, not_10_out, or_1_out, or_2_out;

  not not_1 (not_1_out, out_8);
  T_Flip_Flop t_ff_1 (.clk(not_1_out), .T(in_1), .Q(out_7), .reset(buffer_1_out));  // open: Qn, preset, en
  T_Flip_Flop t_ff_2 (.clk(not_2_out), .T(in_1), .Q(out_8), .reset(buffer_1_out));  // open: Qn, preset, en
  not not_2 (not_2_out, out_9);
  not not_3 (not_3_out, or_2_out);
  T_Flip_Flop t_ff_3 (.clk(not_3_out), .T(in_1), .Q(out_9), .reset(buffer_1_out));  // open: Qn, preset, en
  not not_4 (out_6, in_1);
  and and_1 (out_5, out_7, out_8, not_5_out);
  not not_5 (not_5_out, out_9);
  buf buffer_1 (buffer_1_out, out_5);
  not not_6 (not_6_out, out_11);
  not not_7 (not_7_out, out_12);
  not not_8 (not_8_out, out_13);
  or or_1 (or_1_out, in_2, in_4);
  T_Flip_Flop t_ff_4 (.clk(not_6_out), .T(in_1), .Q(out_10), .reset(buffer_2_out));  // open: Qn, preset, en
  T_Flip_Flop t_ff_5 (.clk(not_7_out), .T(in_1), .Q(out_11), .reset(buffer_2_out));  // open: Qn, preset, en
  T_Flip_Flop t_ff_6 (.clk(not_8_out), .T(in_1), .Q(out_12), .reset(buffer_2_out));  // open: Qn, preset, en
  T_Flip_Flop t_ff_7 (.clk(or_1_out), .T(in_1), .Q(out_13), .reset(buffer_2_out));  // open: Qn, preset, en
  not not_9 (not_9_out, out_11);
  not not_10 (not_10_out, out_13);
  or or_2 (or_2_out, and_2_out, in_3);
  and and_2 (and_2_out, out_10, not_9_out, out_12, not_10_out);
  buf buffer_2 (buffer_2_out, and_2_out);
endmodule

module _24hour (
  input  in_1,
  input  in_2,
  input  in_3,
  output out_4,
  output out_5,
  output out_6,
  output out_7,
  output out_8,
  output out_9,
  output out_10,
  output out_11
);

  wire and_1_out, and_2_out, and_3_out, not_1_out, not_2_out, not_4_out, not_5_out, not_6_out, not_7_out,
       not_8_out, not_9_out, not_10_out, not_11_out, not_12_out, not_13_out, or_1_out, or_2_out;

  not not_1 (not_1_out, out_7);
  T_Flip_Flop t_ff_1 (.clk(not_1_out), .T(in_1), .Q(out_6), .reset(and_1_out));  // open: Qn, preset, en
  T_Flip_Flop t_ff_2 (.clk(not_2_out), .T(in_1), .Q(out_7), .reset(and_1_out));  // open: Qn, preset, en
  not not_2 (not_2_out, and_3_out);
  not not_3 (out_4, in_1);
  and and_1 (and_1_out, out_6, not_4_out, not_7_out, not_6_out, out_9, not_5_out);
  not not_4 (not_4_out, out_7);
  not not_5 (not_5_out, out_8);
  not not_6 (not_6_out, out_10);
  not not_7 (not_7_out, out_11);
  not not_8 (not_8_out, out_9);
  buf and_2 (and_2_out, or_2_out);  // AND_Gate
  not not_9 (not_9_out, out_10);
  not not_10 (not_10_out, out_11);
  or or_1 (or_1_out, in_2, in_3);
  not not_11 (not_11_out, or_1_out);
  T_Flip_Flop t_ff_3 (.clk(not_8_out), .T(in_1), .Q(out_8), .reset(and_2_out));  // open: Qn, preset, en
  T_Flip_Flop t_ff_4 (.clk(not_9_out), .T(in_1), .Q(out_9), .reset(or_2_out));  // open: Qn, preset, en
  T_Flip_Flop t_ff_5 (.clk(not_10_out), .T(in_1), .Q(out_10), .reset(or_2_out));  // open: Qn, preset, en
  T_Flip_Flop t_ff_6 (.clk(not_11_out), .T(in_1), .Q(out_11), .reset(or_2_out));  // open: Qn, preset, en
  not not_12 (not_12_out, out_9);
  and and_3 (and_3_out, out_8, not_12_out, out_10, not_13_out);
  not not_13 (not_13_out, out_11);
  or or_2 (or_2_out, and_3_out, and_1_out);

  assign out_5 = out_4;
endmodule

module _12hour (
  input  in_1,
  input  in_2,
  input  in_3,
  output out_4,
  output out_5,
  output out_6,
  output out_7,
  output out_8,
  output out_9,
  output out_10
);

  wire and_1_out, and_2_out, buffer_1_out, not_1_out, not_2_out, not_3_out, not_4_out, not_5_out, not_6_out,
       not_7_out, not_8_out, not_9_out, not_10_out, or_1_out, or_2_out;

  not not_1 (not_1_out, buffer_1_out);
  T_Flip_Flop t_ff_1 (.clk(not_1_out), .T(in_1), .Q(out_4), .reset(or_2_out));  // open: Qn, preset, en
  or or_1 (or_1_out, in_2, in_3);
  not not_2 (not_2_out, out_6);
  not not_3 (not_3_out, out_7);
  not not_4 (not_4_out, out_8);
  T_Flip_Flop t_ff_2 (.clk(and_2_out), .T(in_1), .Q(out_9), .Qn(out_10));  // open: preset, reset, en
  T_Flip_Flop t_ff_3 (.clk(not_2_out), .T(in_1), .Q(out_5), .reset(or_2_out));  // open: Qn, preset, en
  T_Flip_Flop t_ff_4 (.clk(not_3_out), .T(in_1), .Q(out_6), .reset(or_2_out));  // open: Qn, preset, en
  T_Flip_Flop t_ff_5 (.clk(not_4_out), .T(in_1), .Q(out_7), .reset(or_2_out));  // open: Qn, preset, en
  T_Flip_Flop t_ff_6 (.clk(not_5_out), .T(in_1), .Q(out_8), .reset(or_2_out));  // open: Qn, preset, en
  not not_5 (not_5_out, or_1_out);
  not not_6 (not_6_out, out_6);
  not not_7 (not_7_out, out_8);
  not not_8 (not_8_out, out_5);
  not not_9 (not_9_out, out_6);
  not not_10 (not_10_out, out_8);
  and and_1 (and_1_out, out_5, not_6_out, out_7, not_7_out);
  buf buffer_1 (buffer_1_out, and_1_out);
  and and_2 (and_2_out, not_8_out, not_9_out, out_7, not_10_out, out_4);
  or or_2 (or_2_out, and_2_out, buffer_1_out);
endmodule

module _12or24 (
  input  in_1,
  input  in_2,
  input  in_3,
  input  in_4,
  output out_5,
  output out_6,
  output out_7,
  output out_8,
  output out_9,
  output out_10,
  output out_11,
  output out_12,
  output out_13,
  output out_14
);

  wire n12hour_1_out_4, n12hour_1_out_5, n12hour_1_out_6, n12hour_1_out_7, n12hour_1_out_8, n12hour_1_out_9,
       n12hour_1_out_10, n24hour_1_out_4, n24hour_1_out_5, n24hour_1_out_6, n24hour_1_out_7, n24hour_1_out_8,
       n24hour_1_out_9, n24hour_1_out_10, n24hour_1_out_11, not_1_out, not_2_out, not_3_out, not_4_out,
       not_5_out;

  _24hour u_24hour_1 (
    .in_1(in_2), .in_2(in_4), .out_4(n24hour_1_out_4), .out_5(n24hour_1_out_5), .out_6(n24hour_1_out_6),
    .out_7(n24hour_1_out_7), .out_8(n24hour_1_out_8), .out_9(n24hour_1_out_9), .out_10(n24hour_1_out_10),
    .out_11(n24hour_1_out_11), .in_3(in_3));
  _12hour u_12hour_1 (
    .in_1(in_2), .in_2(in_4), .out_4(n12hour_1_out_4), .out_5(n12hour_1_out_5), .out_6(n12hour_1_out_6),
    .out_7(n12hour_1_out_7), .out_8(n12hour_1_out_8), .out_10(n12hour_1_out_10), .out_9(n12hour_1_out_9),
    .in_3(in_3));
  not not_1 (not_1_out, in_2);
  not not_2 (not_2_out, in_2);
  not not_3 (not_3_out, in_2);
  Multiplexer multiplexer_1 (.in0(n12hour_1_out_8), .in1(n24hour_1_out_11), .out(out_7), .sel(in_1));  // open: en
  Multiplexer multiplexer_2 (.in0(n12hour_1_out_7), .in1(n24hour_1_out_10), .out(out_8), .sel(in_1));  // open: en
  Multiplexer multiplexer_3 (.in0(n12hour_1_out_6), .in1(n24hour_1_out_9), .out(out_9), .sel(in_1));  // open: en
  Multiplexer multiplexer_4 (.in0(n12hour_1_out_5), .in1(n24hour_1_out_8), .out(out_10), .sel(in_1));  // open: en
  Multiplexer multiplexer_5 (.in0(n12hour_1_out_4), .in1(n24hour_1_out_7), .out(out_11), .sel(in_1));  // open: en
  Multiplexer multiplexer_6 (.in0(not_1_out), .in1(n24hour_1_out_6), .out(out_12), .sel(in_1));  // open: en
  Multiplexer multiplexer_7 (.in0(not_2_out), .in1(n24hour_1_out_5), .out(out_13), .sel(in_1));  // open: en
  Multiplexer multiplexer_8 (.in0(not_3_out), .in1(n24hour_1_out_4), .out(out_14), .sel(in_1));  // open: en
  and and_1 (out_5, n12hour_1_out_10, not_4_out);
  not not_4 (not_4_out, in_1);
  not not_5 (not_5_out, in_1);
  and and_2 (out_6, n12hour_1_out_9, not_5_out);
endmodule

module decoder (
  input  Q,
  input  W,
  input  E,
  input  R,
  output out_5,
  output out_6,
  output out_7,
  output out_8,
  output out_9,
  output out_10,
  output out_11
);

  wire and_1_out, and_2_out, nor_1_out, nor_2_out, nor_3_out, not_1_out, not_2_out, not_3_out, not_4_out,
       not_5_out, xnor_1_out, xnor_2_out, xnor_3_out, xor_1_out, xor_2_out, xor_3_out;

  and and_1 (and_1_out, E, not_1_out);
  not not_1 (not_1_out, R);
  ExactlyOne xor_1 (.out(xor_1_out), .in0(Q), .in1(W), .in2(E));
  nor nor_1 (nor_1_out, E, R);
  xnor xnor_1 (xnor_1_out, W, R);
  not not_2 (not_2_out, W);
  xnor xnor_2 (xnor_2_out, E, R);
  not not_3 (not_3_out, W);
  not not_4 (not_4_out, R);
  xor xor_2 (xor_2_out, Q, W);
  xor xor_3 (xor_3_out, E, R);
  nor nor_2 (nor_2_out, W, R);
  nor nor_3 (nor_3_out, W, R);
  and and_2 (and_2_out, E, not_5_out);
  not not_5 (not_5_out, R);
  or or_1 (out_5, and_1_out, xor_1_out);
  or or_2 (out_6, Q, W, nor_1_out);
  or or_3 (out_7, Q, E, xnor_1_out);
  or or_4 (out_8, not_2_out, xnor_2_out);
  nand nand_1 (out_9, E, not_3_out, not_4_out);
  xnor xnor_3 (xnor_3_out, xor_2_out, xor_3_out);
  or or_5 (out_11, nor_3_out, and_2_out);
  or or_6 (out_10, xnor_3_out, nor_2_out);
endmodule

module fan_pwer (
  input  in_1,
  input  in_2,
  input  in_3,
  input  in_4,
  input  in_5,
  output Leve1_LED,
  output Level2_LED,
  output Level3_LED,
  output Rotation
);

  wire and_1_out, not_1_out, or_1_out, or_2_out, or_3_out, or_4_out;

  not not_1 (not_1_out, in_1);
  or or_1 (or_1_out, in_3, in_4, not_1_out);
  or or_2 (or_2_out, in_2, in_4, not_1_out);
  or or_3 (or_3_out, in_2, in_3, not_1_out);
  T_Flip_Flop t_ff_1 (.clk(in_2), .T(in_1), .Q(Leve1_LED), .reset(or_1_out));  // open: Qn, preset, en
  T_Flip_Flop t_ff_2 (.clk(in_3), .T(in_1), .Q(Level2_LED), .reset(or_2_out));  // open: Qn, preset, en
  T_Flip_Flop t_ff_3 (.clk(in_4), .T(in_1), .Q(Level3_LED), .reset(or_3_out));  // open: Qn, preset, en
  and and_1 (and_1_out, or_4_out, in_5);
  T_Flip_Flop t_ff_4 (.clk(and_1_out), .T(in_1), .Q(Rotation), .reset(not_1_out));  // open: Qn, preset, en
  or or_4 (or_4_out, Leve1_LED, Level2_LED, Level3_LED);
endmodule

module sec_clk (
  input  power,
  input  plus_10,
  input  plus_1,
  output plus_min,
  output out_5,
  output out_6,
  output out_7,
  output out_8,
  output out_9,
  output out_10,
  output out_11,
  output out_12,
  output out_13,
  output out_14,
  output out_15,
  output out_16,
  output out_17,
  output out_18
);

  wire clock_1_out, sec_min_out_6, sec_min_out_7, sec_min_out_8, sec_min_out_9, sec_min_out_10,
       sec_min_out_11, sec_min_out_12, sec_min_out_13;

  Clock clock_1 (.out(clock_1_out));
  Sec_min sec_min (
    .in_1(power), .in_2(clock_1_out), .out_5(plus_min), .out_6(sec_min_out_6), .out_7(sec_min_out_7),
    .out_8(sec_min_out_8), .out_9(sec_min_out_9), .out_10(sec_min_out_10), .out_11(sec_min_out_11),
    .out_12(sec_min_out_12), .out_13(sec_min_out_13), .in_3(plus_10), .in_4(plus_1));
  decoder decoder (
    .Q(sec_min_out_10), .W(sec_min_out_11), .E(sec_min_out_12), .R(sec_min_out_13), .out_5(out_8),
    .out_6(out_9), .out_7(out_10), .out_8(out_11), .out_9(out_7), .out_10(out_6), .out_11(out_5));
  decoder decoder_2 (
    .Q(sec_min_out_6), .W(sec_min_out_7), .E(sec_min_out_8), .R(sec_min_out_9), .out_5(out_15),
    .out_6(out_16), .out_7(out_17), .out_8(out_18), .out_9(out_14), .out_10(out_13), .out_11(out_12));
endmodule

module min_clk (
  input  power,
  input  plus_min,
  input  plus_10,
  input  plus_1,
  output plus_hour,
  output out_6,
  output out_7,
  output out_8,
  output out_9,
  output out_10,
  output out_11,
  output out_12,
  output out_13,
  output out_14,
  output out_15,
  output out_16,
  output out_17,
  output out_18,
  output out_19
);

  wire sec_min_out_6, sec_min_out_7, sec_min_out_8, sec_min_out_9, sec_min_out_10, sec_min_out_11,
       sec_min_out_12, sec_min_out_13;

  Sec_min sec_min (
    .in_1(power), .in_2(plus_min), .out_5(plus_hour), .out_6(sec_min_out_6), .out_7(sec_min_out_7),
    .out_8(sec_min_out_8), .out_9(sec_min_out_9), .out_10(sec_min_out_10), .out_11(sec_min_out_11),
    .out_12(sec_min_out_12), .out_13(sec_min_out_13), .in_3(plus_10), .in_4(plus_1));
  decoder decoder (
    .Q(sec_min_out_10), .W(sec_min_out_11), .E(sec_min_out_12), .R(sec_min_out_13), .out_5(out_10),
    .out_6(out_11), .out_7(out_12), .out_8(out_13), .out_9(out_19), .out_10(out_18), .out_11(out_17));
  decoder decoder_2 (
    .Q(sec_min_out_6), .W(sec_min_out_7), .E(sec_min_out_8), .R(sec_min_out_9), .out_5(out_6), .out_6(out_7),
    .out_7(out_8), .out_8(out_9), .out_9(out_16), .out_10(out_15), .out_11(out_14));
endmodule

module hour_clk (
  input  _12_24,
  input  power,
  input  plus_1hour,
  input  plus_1,
  output am,
  output out_6,
  output out_7,
  output out_8,
  output out_9,
  output out_10,
  output out_11,
  output out_12,
  output out_13,
  output pm,
  output out_15,
  output out_16,
  output out_17,
  output out_18,
  output out_19,
  output out_20
);

  wire _12_or_24_out_7, _12_or_24_out_8, _12_or_24_out_9, _12_or_24_out_10, _12_or_24_out_11,
       _12_or_24_out_12, _12_or_24_out_13, _12_or_24_out_14;

  _12or24 _12_or_24 (
    .in_2(power), .in_4(plus_1hour), .in_1(_12_24), .out_14(_12_or_24_out_14), .out_13(_12_or_24_out_13),
    .out_12(_12_or_24_out_12), .out_11(_12_or_24_out_11), .out_10(_12_or_24_out_10), .out_9(_12_or_24_out_9),
    .out_8(_12_or_24_out_8), .out_7(_12_or_24_out_7), .out_5(am), .out_6(pm), .in_3(plus_1));
  decoder decoder (
    .Q(_12_or_24_out_10), .W(_12_or_24_out_9), .E(_12_or_24_out_8), .R(_12_or_24_out_7), .out_5(out_10),
    .out_6(out_11), .out_7(out_12), .out_8(out_13), .out_9(out_20), .out_10(out_19), .out_11(out_18));
  decoder decoder_2 (
    .Q(_12_or_24_out_14), .W(_12_or_24_out_13), .E(_12_or_24_out_12), .R(_12_or_24_out_11), .out_5(out_6),
    .out_6(out_7), .out_7(out_8), .out_8(out_9), .out_9(out_17), .out_10(out_16), .out_11(out_15));
endmodule

module set_time (
  input  power,
  input  add30,
  output [8:0] out_3
);

  wire comparator_1_eq, not_1_out;
  wire [8:0] adder_1_out, multiplexer_1_out;

  not not_1 (not_1_out, power);
  Register #(.width(9)) register_1 (.D(multiplexer_1_out), .en(power), .Q(out_3), .clk(add30), .clr(not_1_out));
  Adder #(.width(9)) adder_1 (.a(out_3), .b(9'h1e), .out(adder_1_out));  // open: cin, cout
  Comparator #(.width(9)) comparator_1 (.a(out_3), .b(9'h168), .eq(comparator_1_eq));  // open: gt, lt
  Multiplexer #(.width(9)) multiplexer_1 (
    .in0(adder_1_out), .in1({9{1'b0}}), .out(multiplexer_1_out), .sel(comparator_1_eq));  // open: en
endmodule

module timer_dec (
  input  [8:0] in_1,
  output [3:0] out_2,
  output [3:0] out_3,
  output [3:0] out_4
);

  wire [8:0] divider_1_out, divider_1_rem;

  Divider #(.width(9)) divider_1 (.a(in_1), .b(9'h3c), .out(divider_1_out), .rem(divider_1_rem));  // open: upper
  ROM #(.addrWidth(9), .dataWidth(4)) rom_1 (.addr(divider_1_out), .data(out_2));  // open: sel
  ROM #(.addrWidth(9)) rom_2 (.addr(divider_1_rem), .data({out_3, out_4}));  // open: sel

  // Notes on the sheet:
  //   contents of rom_1 (hex, n*v repeats v):
  //   0 1 2 3 4 5 6
  //   contents of rom_2 (hex, n*v repeats v):
  //   0 1 2 3 4 5 6 7 8 9 10 11 12 13 14 15 16 17 18 19 20 21 22 23 24 25 26 27 28 29 30 31 32 33 34 35 36
  //   37 38 39 40 41 42 43 44 45 46 47 48 49 50 51 52 53 54 55 56 57 58 59
endmodule
