// Logisim project timercirucit1.circ as structural Verilog: 2 circuits, main circuit main
module main (
);

  wire clock_1_out, comparator_1_eq, not_1_out, not_2_out, or_1_out, reset_out, time_selecter_out,
       timer_start_out;
  wire [3:0] counter_1_q, time_select_out_2;

  Button timer_start (.out(timer_start_out));
  Button time_selecter (.out(time_selecter_out));
  Clock #(.lowDuration(59)) clock_1 (.out(clock_1_out));
  sel time_select (.in_1(time_selecter_out), .out_2(time_select_out_2));
  not not_1 (not_1_out, timer_start_out);
  Hex_Digit_Display hex_digit_display_1 (.value(time_select_out_2));  // open: dp
  or or_1 (or_1_out, timer_start_out, clock_1_out);
  Button reset (.out(reset_out));
  Counter #(.width(4), .max('hf), .ongoal("stay")) counter_1 (
    .load(1'b1), .D(time_select_out_2), .count(not_1_out), .Q(counter_1_q), .clk(or_1_out), .clr(reset_out));  // open: carry
  Hex_Digit_Display hex_digit_display_2 (.value(counter_1_q), .dp(not_2_out));
  not not_2 (not_2_out, comparator_1_eq);
  Comparator #(.width(4)) comparator_1 (.a(counter_1_q), .b(4'b0000), .eq(comparator_1_eq));  // open: gt, lt
endmodule

module sel (
  input  in_1,
  output [3:0] out_2
);

  wire comparator_1_eq, reset_out;
  wire [3:0] adder_1_out, multiplexer_1_out;

  Button reset (.out(reset_out));
  Register #(.width(4)) register_1 (.D(multiplexer_1_out), .Q(out_2), .clk(in_1), .clr(reset_out));  // open: en
  Adder #(.width(4)) adder_1 (.a(out_2), .b(4'b0001), .out(adder_1_out));  // open: cin, cout
  Comparator #(.width(4)) comparator_1 (.a(out_2), .b(4'b0110), .eq(comparator_1_eq));  // open: gt, lt
  Multiplexer #(.width(4)) multiplexer_1 (
    .in0(adder_1_out), .in1(4'b0000), .out(multiplexer_1_out), .sel(comparator_1_eq));  // open: en
endmodule
